# Fritzing sketch EE_OpenBot-Arduino-Servo (saved by Fritzing 0.9.3b)
breadboards: 1

parts:
  Componente1 = Arduino Nano (Rev3.0)
  J1 = Basic Servo
  VCC1 = 4 x AAA Battery Mount
  X1 = USB Connectors [package=usb-mb-h]  # not connected

nets:
  GND: Componente1.GND, J1.gnd, VCC1.-
  N1: Componente1.A0, J1.pulse
  N2: J1.vcc, VCC1.+
